# Fritzing sketch SHK-SterilizatorProstorije (saved by Fritzing 0.9.3b)
breadboards: 1

parts:
  Part1 = Arduino Uno (Rev3) - ICSP
  U1 = LCD-16X2 [package=lcd-16x2_noholes]
  LCM1602_IIC1 = LCM1602 IIC [part_number="LCM1602 IIC" chip_label="LCM1602 IIC" package="DIP (Dual Inline) [THT]"]
  LED1 = LED - 5mm [color="Red (633nm)" package="5 mm [THT]"]
  R1 = Resistor [tolerance=±5% resistance=220 package="2010 [SMD]"]
  microSD1 = MicroSD Card Module
  MPX1 = MPX2010 pressure sensor [part_number=MPX]
  MPX2 = MPX2010 pressure sensor [part_number=MPX]

nets:
  N1: Part1.A1, MPX1.V_out_-
  N2: Part1.A2, MPX2.V_out_-
  N3: Part1.A4/SDA, LCM1602_IIC1.SDA
  N4: Part1.A5/SCL, LCM1602_IIC1.SCL
  N5: Part1.D11_PWM/MOSI, microSD1.MOSI
  N6: Part1.D12/MISO, microSD1.MISO
  N7: Part1.D13/SCK, microSD1.SCK
  N8: Part1.D3_PWM, LED1.anode
  N9: Part1.D4, microSD1.CS
  VCC: Part1.5V, LCM1602_IIC1.VCC, microSD1.VCC, MPX1.Vs, MPX2.Vs
  GND: Part1.GND, LCM1602_IIC1.GND, LED1.cathode, R1.Pin_0, R1.Pin_1, microSD1.GND, MPX1.V_out_+, MPX2.V_out_+
  VSS: U1.VSS, LCM1602_IIC1.VSS
  VDD: U1.VDD, LCM1602_IIC1.VDD
  N10: U1.VO, LCM1602_IIC1.V0
  N11: U1.RS, LCM1602_IIC1.RS
  N12: U1.R_W, LCM1602_IIC1.RW
  N13: U1.E, LCM1602_IIC1.E
  N14: U1.DB0, LCM1602_IIC1.D0
  N15: U1.DB1, LCM1602_IIC1.D1
  N16: U1.DB2, LCM1602_IIC1.D2
  N17: U1.DB3, LCM1602_IIC1.D3
  N18: U1.DB4, LCM1602_IIC1.D4
  N19: U1.DB5, LCM1602_IIC1.D5
  N20: U1.DB6, LCM1602_IIC1.D6
  N21: U1.DB7, LCM1602_IIC1.D7
  N22: U1.A, LCM1602_IIC1.A
  N23: U1.K, LCM1602_IIC1.K

custom parts:
  LCM1602 IIC: I2C-Module to use a 1602 or 2004 LCD on with the wire.h libory Serial LCD Modul
